# Fritzing sketch ESP32&2.2Display (saved by Fritzing 0.9.3b)
breadboards: 2

parts:
  U1 = ESP32S-HiLetgo [part_number=ESP32S-HiLetgo]
  TFT1 = Color 320x240 TFT Display, ILI9341 Controller Chip

nets:
  N1: U1.3.3, TFT1.VCC, TFT1.LED
  GND: U1.GND, TFT1.GND
  N2: U1.GPIO16, TFT1.D/C
  N3: U1.GPIO17, TFT1.Reset
  N4: U1.GPIO5, TFT1.CS
  N5: U1.GPIO18, TFT1.SCK
  N6: U1.GPIO19, TFT1.SDO_(MISO)
  N7: U1.GPIO23, TFT1.SDI_(MOSI)

custom parts:
  ESP32S-HiLetgo: HiLetgo ESP-WROOM-32 ESP32 ESP-32S Development Board 2.4GHz Dual-Mode WiFi + Bluetooth Dual Cores Microcontroller The ESP32 integrated with Antenna switches, RF Balun, power amplifiers, low-noise amplifiers, filters, and management modules, and the entire solution occupies the least area of PCB. 2.4 GHz Wi-Fi plus Bluetooth dual-mode chip, with TSMC Ultra-low power consumption 40nm technology,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
  Color 320x240 TFT Display, ILI9341 Controller Chip: 2.2" TFT Display with ILI9341 Controller
